// Logisim project cpu.circ as structural Verilog: 3 circuits, main circuit main
module main (
);

  wire clock_1_out, dipswitch_1_sw7, dipswitch_1_sw8, instruction_spliter_1_out_6,
       instruction_spliter_1_out_7, instruction_spliter_1_out_8, instruction_spliter_1_out_9,
       instruction_spliter_1_out_10, instruction_spliter_1_out_11, instruction_spliter_1_out_12,
       instruction_spliter_1_out_13, instruction_spliter_1_out_14, instruction_spliter_1_out_15,
       instruction_spliter_1_out_16, instruction_spliter_1_out_17, instruction_spliter_1_out_18,
       instruction_spliter_1_out_19, instruction_spliter_1_out_20, instruction_spliter_1_out_21,
       instruction_spliter_1_out_22, instruction_spliter_1_out_23, instruction_spliter_1_out_24,
       instruction_spliter_1_out_25, instruction_spliter_1_out_26, instruction_spliter_1_out_27,
       instruction_spliter_1_out_28, instruction_spliter_1_out_29, instruction_spliter_1_out_30,
       instruction_spliter_1_out_31, instruction_spliter_1_out_32, instruction_spliter_1_out_33,
       instruction_spliter_1_out_34, instruction_spliter_1_out_35, instruction_spliter_1_out_36,
       instruction_spliter_1_out_37, instruction_spliter_1_out_38, instruction_spliter_1_out_39,
       instruction_spliter_1_out_40, instruction_spliter_1_out_41, instruction_spliter_1_out_42,
       instruction_spliter_1_out_43, instruction_spliter_1_out_44, instruction_spliter_1_out_45,
       instruction_spliter_1_out_46, instruction_spliter_1_out_47, instruction_spliter_1_out_48,
       instruction_spliter_1_out_49, instruction_spliter_1_out_50, instruction_spliter_1_out_51,
       instruction_spliter_1_out_52, instruction_spliter_1_out_53, instruction_spliter_1_out_54,
       instruction_spliter_1_out_55, instruction_spliter_1_out_56, instruction_spliter_1_out_57,
       instruction_spliter_1_out_58, instruction_spliter_1_out_59, instruction_spliter_1_out_60,
       instruction_spliter_1_out_61, instruction_spliter_1_out_62, instruction_spliter_1_out_63,
       instruction_spliter_1_out_64, instruction_spliter_1_out_65;
  wire [7:0] counter_1_q, instruction_spliter_1_p1, instruction_spliter_1_p2_l, instruction_spliter_1_p2_u;
  wire [15:0] instruction_spliter_1_p2;
  wire [39:0] rom_1_data;

  ROM #(.dataWidth(40)) rom_1 (.addr(counter_1_q), .data(rom_1_data));
  DipSwitch dipswitch_1 (.sw7(dipswitch_1_sw7), .sw8(dipswitch_1_sw8));  // open: sw1, sw2, sw3, sw4, sw5, sw6
  Counter counter_1 (
    .clr(dipswitch_1_sw7), .up(1'b1), .count(dipswitch_1_sw8), .clk(clock_1_out), .Q(counter_1_q));  // open: load, D, carry
  Clock clock_1 (.out(clock_1_out));
  Instruction_Spliter instruction_spliter_1 (
    .Instruction(rom_1_data), .P2(instruction_spliter_1_p2), .P2_L(instruction_spliter_1_p2_l),
    .P2_U(instruction_spliter_1_p2_u), .P1(instruction_spliter_1_p1), .out_6(instruction_spliter_1_out_6),
    .out_7(instruction_spliter_1_out_7), .out_8(instruction_spliter_1_out_8),
    .out_9(instruction_spliter_1_out_9), .out_10(instruction_spliter_1_out_10),
    .out_11(instruction_spliter_1_out_11), .out_12(instruction_spliter_1_out_12),
    .out_13(instruction_spliter_1_out_13), .out_14(instruction_spliter_1_out_14),
    .out_15(instruction_spliter_1_out_15), .out_16(instruction_spliter_1_out_16),
    .out_17(instruction_spliter_1_out_17), .out_18(instruction_spliter_1_out_18),
    .out_19(instruction_spliter_1_out_19), .out_20(instruction_spliter_1_out_20),
    .out_21(instruction_spliter_1_out_21), .out_22(instruction_spliter_1_out_22),
    .out_23(instruction_spliter_1_out_23), .out_24(instruction_spliter_1_out_24),
    .out_25(instruction_spliter_1_out_25), .out_26(instruction_spliter_1_out_26),
    .out_27(instruction_spliter_1_out_27), .out_28(instruction_spliter_1_out_28),
    .out_29(instruction_spliter_1_out_29), .out_30(instruction_spliter_1_out_30),
    .out_31(instruction_spliter_1_out_31), .out_32(instruction_spliter_1_out_32),
    .out_33(instruction_spliter_1_out_33), .out_34(instruction_spliter_1_out_34),
    .out_35(instruction_spliter_1_out_35), .out_36(instruction_spliter_1_out_36),
    .out_37(instruction_spliter_1_out_37), .out_38(instruction_spliter_1_out_38),
    .out_39(instruction_spliter_1_out_39), .out_40(instruction_spliter_1_out_40),
    .out_41(instruction_spliter_1_out_41), .out_42(instruction_spliter_1_out_42),
    .out_43(instruction_spliter_1_out_43), .out_44(instruction_spliter_1_out_44),
    .out_45(instruction_spliter_1_out_45), .out_46(instruction_spliter_1_out_46),
    .out_47(instruction_spliter_1_out_47), .out_48(instruction_spliter_1_out_48),
    .out_49(instruction_spliter_1_out_49), .out_50(instruction_spliter_1_out_50),
    .out_51(instruction_spliter_1_out_51), .out_52(instruction_spliter_1_out_52),
    .out_53(instruction_spliter_1_out_53), .out_54(instruction_spliter_1_out_54),
    .out_55(instruction_spliter_1_out_55), .out_56(instruction_spliter_1_out_56),
    .out_57(instruction_spliter_1_out_57), .out_58(instruction_spliter_1_out_58),
    .out_59(instruction_spliter_1_out_59), .out_60(instruction_spliter_1_out_60),
    .out_61(instruction_spliter_1_out_61), .out_62(instruction_spliter_1_out_62),
    .out_63(instruction_spliter_1_out_63), .out_64(instruction_spliter_1_out_64),
    .out_65(instruction_spliter_1_out_65));
  // Probe on instruction_spliter_1_p2
  // Probe on instruction_spliter_1_p2_l
  // Probe on instruction_spliter_1_p1
  // Probe on instruction_spliter_1_out_6
  // Probe on instruction_spliter_1_out_7
  // Probe on instruction_spliter_1_out_8
  // Probe on instruction_spliter_1_out_9
  // Probe on instruction_spliter_1_out_10
  // Probe on instruction_spliter_1_out_11
  // Probe on instruction_spliter_1_out_12
  // Probe on instruction_spliter_1_out_13
  // Probe on instruction_spliter_1_out_14
  // Probe on instruction_spliter_1_out_15
  // Probe on instruction_spliter_1_out_16
  // Probe on instruction_spliter_1_out_17
  // Probe on instruction_spliter_1_out_18
  // Probe on instruction_spliter_1_out_19
  // Probe on instruction_spliter_1_out_20
  // Probe on instruction_spliter_1_out_21
  // Probe on instruction_spliter_1_out_22
  // Probe on instruction_spliter_1_out_23
  // Probe on instruction_spliter_1_out_24
  // Probe on instruction_spliter_1_out_25
  // Probe on instruction_spliter_1_out_26
  // Probe on instruction_spliter_1_out_27
  // Probe on instruction_spliter_1_out_28
  // Probe on instruction_spliter_1_out_29
  // Probe on instruction_spliter_1_out_30
  // Probe on instruction_spliter_1_out_31
  // Probe on instruction_spliter_1_out_32
  // Probe on instruction_spliter_1_out_33
  // Probe on instruction_spliter_1_out_34
  // Probe on instruction_spliter_1_out_35
  // Probe on instruction_spliter_1_out_36
  // Probe on instruction_spliter_1_out_37
  // Probe on instruction_spliter_1_out_38
  // Probe on instruction_spliter_1_out_39
  // Probe on instruction_spliter_1_out_40
  // Probe on instruction_spliter_1_out_41
  // Probe on instruction_spliter_1_out_42
  // Probe on instruction_spliter_1_out_43
  // Probe on instruction_spliter_1_out_44
  // Probe on instruction_spliter_1_out_45
  // Probe on instruction_spliter_1_out_46
  // Probe on instruction_spliter_1_out_47
  // Probe on instruction_spliter_1_out_48
  // Probe on instruction_spliter_1_out_49
  // Probe on instruction_spliter_1_out_50
  // Probe on instruction_spliter_1_out_51
  // Probe on instruction_spliter_1_out_52
  // Probe on instruction_spliter_1_out_53
  // Probe on instruction_spliter_1_out_54
  // Probe on instruction_spliter_1_out_55
  // Probe on instruction_spliter_1_out_56
  // Probe on instruction_spliter_1_out_57
  // Probe on instruction_spliter_1_out_58
  // Probe on instruction_spliter_1_out_59
  // Probe on instruction_spliter_1_out_60
  // Probe on instruction_spliter_1_out_61
  // Probe on instruction_spliter_1_out_62
  // Probe on instruction_spliter_1_out_63
  // Probe on instruction_spliter_1_out_64
  // Probe on instruction_spliter_1_out_65
  // Probe on instruction_spliter_1_p2_u

  // Notes on the sheet:
  //   contents of rom_1 (hex, n*v repeats v):
  //   33000004 10041 20065 42010002 fffeffffff
endmodule

module Instruction_Spliter (
  input  [39:0] Instruction,
  output [15:0] P2,
  output [7:0] P2_L,
  output [7:0] P2_U,
  output [7:0] P1,
  output out_6,
  output out_7,
  output out_8,
  output out_9,
  output out_10,
  output out_11,
  output out_12,
  output out_13,
  output out_14,
  output out_15,
  output out_16,
  output out_17,
  output out_18,
  output out_19,
  output out_20,
  output out_21,
  output out_22,
  output out_23,
  output out_24,
  output out_25,
  output out_26,
  output out_27,
  output out_28,
  output out_29,
  output out_30,
  output out_31,
  output out_32,
  output out_33,
  output out_34,
  output out_35,
  output out_36,
  output out_37,
  output out_38,
  output out_39,
  output out_40,
  output out_41,
  output out_42,
  output out_43,
  output out_44,
  output out_45,
  output out_46,
  output out_47,
  output out_48,
  output out_49,
  output out_50,
  output out_51,
  output out_52,
  output out_53,
  output out_54,
  output out_55,
  output out_56,
  output out_57,
  output out_58,
  output out_59,
  output out_60,
  output out_61,
  output out_62,
  output out_63,
  output out_64,
  output out_65
);

  // Probe on Instruction[39:24]
  decoder16 decoder16_1 (
    .Data(Instruction[39:24]), .Enable(1'b1), .out_3(out_6), .out_4(out_7), .out_5(out_8), .out_6(out_9),
    .out_7(out_10), .out_8(out_11), .out_9(out_12), .out_10(out_13), .out_11(out_14), .out_12(out_15),
    .out_13(out_16), .out_14(out_17), .out_15(out_18), .out_16(out_19), .out_17(out_20), .out_18(out_21),
    .out_19(out_22), .out_20(out_23), .out_21(out_24), .out_22(out_25), .out_23(out_26), .out_24(out_27),
    .out_25(out_28), .out_26(out_29), .out_27(out_30), .out_28(out_31), .out_29(out_32), .out_30(out_33),
    .out_31(out_34), .out_32(out_35), .out_33(out_36), .out_34(out_37), .out_35(out_38), .out_36(out_39),
    .out_37(out_40), .out_38(out_41), .out_39(out_42), .out_40(out_43), .out_41(out_44), .out_42(out_45),
    .out_43(out_46), .out_44(out_47), .out_45(out_48), .out_46(out_49), .out_47(out_50), .out_48(out_51),
    .out_49(out_52), .out_50(out_53), .out_51(out_54), .out_52(out_55), .out_53(out_56), .out_54(out_57),
    .out_55(out_58), .out_56(out_59), .out_57(out_60), .out_58(out_61), .out_59(out_62), .out_60(out_63),
    .out_61(out_64), .out_62(out_65));

  assign P1 = Instruction[23:16];
  assign P2 = Instruction[15:0];
  assign P2_L = Instruction[7:0];
  assign P2_U = Instruction[15:8];
endmodule

module decoder16 (
  input  [15:0] Data,
  input  Enable,
  output out_3,
  output out_4,
  output out_5,
  output out_6,
  output out_7,
  output out_8,
  output out_9,
  output out_10,
  output out_11,
  output out_12,
  output out_13,
  output out_14,
  output out_15,
  output out_16,
  output out_17,
  output out_18,
  output out_19,
  output out_20,
  output out_21,
  output out_22,
  output out_23,
  output out_24,
  output out_25,
  output out_26,
  output out_27,
  output out_28,
  output out_29,
  output out_30,
  output out_31,
  output out_32,
  output out_33,
  output out_34,
  output out_35,
  output out_36,
  output out_37,
  output out_38,
  output out_39,
  output out_40,
  output out_41,
  output out_42,
  output out_43,
  output out_44,
  output out_45,
  output out_46,
  output out_47,
  output out_48,
  output out_49,
  output out_50,
  output out_51,
  output out_52,
  output out_53,
  output out_54,
  output out_55,
  output out_56,
  output out_57,
  output out_58,
  output out_59,
  output out_60,
  output out_61,
  output out_62
);

  wire and_1_out;

  // Probe on Data[15:12]
  // Probe on Data[11:8]
  // Probe on Data[7:4]
  // Probe on Data[3:0]
  and and_1 (and_1_out, Data[0], Data[1], Data[2], Data[3], Data[4], Data[5], Data[6], Data[7], Data[8], Data[9], Data[10], Data[11], Data[12], Data[13], Data[14], Data[15]);
  Controlled_Buffer controlled_buffer_1 (.in(and_1_out), .en(Enable));  // open: out
endmodule
